# Fritzing sketch BluetoothDisplay (saved by Fritzing 0.9.9b)
breadboards: 1

parts:
  Part1 = Arduino Nano (Rev3.0)
  Part2 = Bluetooth HC-05 Macho
  Part3 = HC-SR501 Body Sensor Module
  Display1 = LCD screen 16x2 IIC [part_number=101290]
  R2 = Resistor [tolerance=±5% resistance=2.2k package="0402 [SMD]"]
  R3 = Resistor [tolerance=±5% power=0.25 resistance=2.2k package=THT]

nets:
  N1: Part1.D1/TX, R2.Pin_0
  N2: Part1.D0/RX, Part2.TXD
  GND: Part1.GND, Part2.GND, Part3.GND, Display1.GND, R3.Pin_1
  N3: Part1.D7, Part3.OUT
  VCC: Part1.5V, Part2.VCC, Part3.VCC, Display1.VCC
  N4: Part1.A5, Display1.SCL
  N5: Part1.A4, Display1.SDA
  N6: Part2.RXD, R2.Pin_1, R3.Pin_0

custom parts:
  HC-SR501 Body Sensor Module: Pyroelectric Infrared PIR Motion Sensor Detector Module
  LCD screen 16x2 IIC: LCD screen with HD44780 controller enables showing text, symbols, value or anything else that comes from Croduino/Arduino. It is capable of showing 16 symbols in two lines and therefore can be used in many projects that need to send clearly visible and legible output information.. • Color of symbols: White • Backlight: Blue • Dimensions: 80 x 36 x 12 mm • Screen dimensions: 64.5 x 16 mm •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
