# Fritzing sketch TempHumiditySensor (saved by Fritzing 0.9.9b)
breadboards: 1

parts:
  Part1 = Arduino Nano (Rev3.0)
  Display1 = LCD screen 16x2 IIC [part_number=101290]
  DHT1 = DHT11 Humitidy and Temperature Sensor
  J1 = Piezo Speaker

nets:
  GND: Part1.GND, Display1.GND, DHT1.GND, J1.pin1
  N1: Part1.D2, DHT1.DATA
  N2: Part1.D5, J1.pin2
  5V: Part1.5V, Display1.VCC, DHT1.VDD
  N3: Part1.A5, Display1.SCL
  N4: Part1.A4, Display1.SDA

custom parts:
  LCD screen 16x2 IIC: LCD screen with HD44780 controller enables showing text, symbols, value or anything else that comes from Croduino/Arduino. It is capable of showing 16 symbols in two lines and therefore can be used in many projects that need to send clearly visible and legible output information.. • Color of symbols: White • Backlight: Blue • Dimensions: 80 x 36 x 12 mm • Screen dimensions: 64.5 x 16 mm •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
  DHT11 Humitidy and Temperature Sensor: DHT11 Humidity and Temperature Sensor
